// Digital circuit BCDadder.dig as structural Verilog
module BCDadder (
  input  [3:0] A,
  input  [3:0] B,
  input  Cin,
  output Cout,
  output [3:0] sum
);

  wire and_1_out, and_2_out, four_bit_adder_1_c_out, four_bit_adder_1_s0, four_bit_adder_1_s1,
       four_bit_adder_1_s2, four_bit_adder_1_s3;

  four_bit_adder four_bit_adder_1 (
    .Cin(Cin), .A0(A[0]), .B0(B[0]), .A1(A[1]), .B1(B[1]), .A2(A[2]), .B2(B[2]), .A3(A[3]), .B3(B[3]),
    .s0(four_bit_adder_1_s0), .s1(four_bit_adder_1_s1), .s2(four_bit_adder_1_s2), .s3(four_bit_adder_1_s3),
    .C_OUT(four_bit_adder_1_c_out));
  and and_1 (and_1_out, four_bit_adder_1_s1, four_bit_adder_1_s3);
  and and_2 (and_2_out, four_bit_adder_1_s2, four_bit_adder_1_s3);
  four_bit_adder four_bit_adder_2 (
    .Cin(1'b0), .A0(1'b0), .B0(four_bit_adder_1_s0), .A1(Cout), .B1(four_bit_adder_1_s1), .A2(Cout),
    .B2(four_bit_adder_1_s2), .A3(1'b0), .B3(four_bit_adder_1_s3), .s0(sum[0]), .s1(sum[1]), .s2(sum[2]),
    .s3(sum[3]));  // open: C_OUT
  or or_1 (Cout, and_1_out, four_bit_adder_1_c_out, and_2_out);
endmodule
