// Digital circuit calculator.dig as structural Verilog
module calculator (
  input  [3:0] DATA,
  input  DA,
  input  CLK,
  output [3:0] D0,
  output [3:0] D1,
  output [3:0] D2,
  output [3:0] D3,
  output [3:0] D4,
  output [3:0] D5,
  output [3:0] D6,
  output [3:0] D7
);

  wire and_1_out, and_2_out, and_3_out, d_ff_1_nq, or_1_out, or_2_out, selector_1__0_9, selector_1_clear,
       selector_1_sum, selector_1_sum_clear;
  wire [3:0] multiplexer_1_out, multiplexer_2_out, multiplexer_3_out, multiplexer_4_out, multiplexer_5_out,
       multiplexer_6_out, multiplexer_7_out, multiplexer_8_out, register_7_q, register_8_q;
  wire [23:0] register_1_q;
  wire [31:0] multiplexer_9_out, summer_1_sum, Y_q;

  selector selector_1 (
    .d(DATA), ._0_9(selector_1__0_9), .clear(selector_1_clear), .sum(selector_1_sum),
    .sum_clear(selector_1_sum_clear));
  D_FF d_ff_1 (.D(DA), .C(CLK), .nQ(d_ff_1_nq));  // open: Q
  and and_1 (and_1_out, selector_1__0_9, DA, d_ff_1_nq);
  and and_2 (and_2_out, DA, d_ff_1_nq, selector_1_sum);
  and and_3 (and_3_out, DA, d_ff_1_nq, selector_1_clear);
  Multiplexer #(.Bits(4)) multiplexer_1 (
    .sel(selector_1_sum_clear), .in_0(DATA), .in_1(4'b0000), .out(multiplexer_1_out));
  Register #(.Bits(4)) register_1 (.D(multiplexer_1_out), .C(CLK), .en(or_2_out), .Q(register_1_q[3:0]));
  Multiplexer #(.Bits(4)) multiplexer_2 (
    .sel(selector_1_sum_clear), .in_0(register_1_q[3:0]), .in_1(4'b0000), .out(multiplexer_2_out));
  Register #(.Bits(4)) register_2 (.D(multiplexer_2_out), .C(CLK), .en(or_2_out), .Q(register_1_q[7:4]));
  Multiplexer #(.Bits(4)) multiplexer_3 (
    .sel(selector_1_sum_clear), .in_0(register_1_q[7:4]), .in_1(4'b0000), .out(multiplexer_3_out));
  Register #(.Bits(4)) register_3 (.D(multiplexer_3_out), .C(CLK), .en(or_2_out), .Q(register_1_q[11:8]));
  or or_1 (or_1_out, and_3_out, and_2_out);
  Multiplexer #(.Bits(4)) multiplexer_4 (
    .sel(selector_1_sum_clear), .in_0(register_1_q[11:8]), .in_1(4'b0000), .out(multiplexer_4_out));
  Register #(.Bits(4)) register_4 (.D(multiplexer_4_out), .C(CLK), .en(or_2_out), .Q(register_1_q[15:12]));
  or or_2 (or_2_out, and_2_out, and_1_out, and_3_out);
  Multiplexer #(.Bits(4)) multiplexer_5 (
    .sel(selector_1_sum_clear), .in_0(register_1_q[15:12]), .in_1(4'b0000), .out(multiplexer_5_out));
  Register #(.Bits(4)) register_5 (.D(multiplexer_5_out), .C(CLK), .en(or_2_out), .Q(register_1_q[19:16]));
  Multiplexer #(.Bits(4)) multiplexer_6 (
    .sel(selector_1_sum_clear), .in_0(register_1_q[19:16]), .in_1(4'b0000), .out(multiplexer_6_out));
  Register #(.Bits(4)) register_6 (.D(multiplexer_6_out), .C(CLK), .en(or_2_out), .Q(register_1_q[23:20]));
  Multiplexer #(.Bits(4)) multiplexer_7 (
    .sel(selector_1_sum_clear), .in_0(register_1_q[23:20]), .in_1(4'b0000), .out(multiplexer_7_out));
  Register #(.Bits(4)) register_7 (.D(multiplexer_7_out), .C(CLK), .en(or_2_out), .Q(register_7_q));
  Multiplexer #(.Bits(4)) multiplexer_8 (
    .sel(selector_1_sum_clear), .in_0(register_7_q), .in_1(4'b0000), .out(multiplexer_8_out));
  Register #(.Bits(4)) register_8 (.D(multiplexer_8_out), .C(CLK), .en(or_2_out), .Q(register_8_q));
  Register #(.Bits(32)) Y (.D(multiplexer_9_out), .C(CLK), .en(or_1_out), .Q(Y_q));
  Multiplexer #(.Bits(32)) multiplexer_9 (
    .sel(selector_1_clear), .in_0(summer_1_sum), .in_1({32{1'b0}}), .out(multiplexer_9_out));
  summer summer_1 (.X({register_8_q, register_7_q, register_1_q}), .Y(Y_q), .sum(summer_1_sum));
  displaySelector displayselector_1 (
    .X({register_8_q, register_7_q, register_1_q}), .Y(Y_q), ._0_9(selector_1__0_9), .sum(selector_1_sum),
    .clk(CLK), .out({D7, D6, D5, D4, D3, D2, D1, D0}));
endmodule
