// Digital circuit displaySelector.dig as structural Verilog
module displaySelector (
  input  [31:0] X,
  input  [31:0] Y,
  input  _0_9,
  input  sum,
  input  clk,
  output [31:0] out
);

  wire and_1_out, and_2_out, d_ff_1_q, not_1_out, or_1_out;

  not not_1 (not_1_out, _0_9);
  and and_1 (and_1_out, d_ff_1_q, not_1_out);
  and and_2 (and_2_out, not_1_out, sum);
  or or_1 (or_1_out, and_1_out, and_2_out);
  D_FF d_ff_1 (.D(or_1_out), .C(clk), .Q(d_ff_1_q));  // open: nQ
  Multiplexer #(.Bits(32)) multiplexer_1 (.sel(d_ff_1_q), .in_0(X), .in_1(Y), .out(out));
endmodule
