// Digital circuit project.dig as structural Verilog
module project (
  input  clk
);

  wire _0_out, _1_out, _2_out, _3_out, _4_out, _5_out, _6_out, _7_out, _8_out, _9_out, A_out, B_out, C_out,
       D_out, E_out, F_out, u_encoder_da;
  wire [3:0] calculator_1_d0, calculator_1_d1, calculator_1_d2, calculator_1_d3, calculator_1_d4,
       calculator_1_d5, calculator_1_d6, calculator_1_d7, u_encoder_data;

  Button _0 (.out(_0_out));
  Button _4 (.out(_4_out));
  Button _8 (.out(_8_out));
  Button C (.out(C_out));
  Button _1 (.out(_1_out));
  Button _5 (.out(_5_out));
  Button _9 (.out(_9_out));
  Button D (.out(D_out));
  Button _2 (.out(_2_out));
  Button _6 (.out(_6_out));
  Button A (.out(A_out));
  Button E (.out(E_out));
  Button _3 (.out(_3_out));
  Button _7 (.out(_7_out));
  Button B (.out(B_out));
  Button F (.out(F_out));
  encoder #(.applicationType("IVERILOG")) u_encoder (
    .P0(_0_out), .P1(_1_out), .P2(_2_out), .P3(_3_out), .P4(_4_out), .P5(_5_out), .P6(_6_out), .P7(_7_out),
    .P8(_8_out), .P9(_9_out), .PA(A_out), .PB(B_out), .PC(C_out), .PD(D_out), .PE(E_out), .PF(F_out),
    .CLK(clk), .DATA(u_encoder_data), .DA(u_encoder_da));
  calculator calculator_1 (
    .DATA(u_encoder_data), .DA(u_encoder_da), .CLK(clk), .D0(calculator_1_d0), .D1(calculator_1_d1),
    .D2(calculator_1_d2), .D3(calculator_1_d3), .D4(calculator_1_d4), .D5(calculator_1_d5),
    .D6(calculator_1_d6), .D7(calculator_1_d7));
  Seven_Seg_Hex seven_seg_hex_1 (.d(calculator_1_d7), .dp(1'b0));
  Seven_Seg_Hex seven_seg_hex_2 (.d(calculator_1_d6), .dp(1'b0));
  Seven_Seg_Hex seven_seg_hex_3 (.d(calculator_1_d5), .dp(1'b0));
  Seven_Seg_Hex seven_seg_hex_4 (.d(calculator_1_d4), .dp(1'b0));
  Seven_Seg_Hex seven_seg_hex_5 (.d(calculator_1_d3), .dp(1'b0));
  Seven_Seg_Hex seven_seg_hex_6 (.d(calculator_1_d2), .dp(1'b0));
  Seven_Seg_Hex seven_seg_hex_7 (.d(calculator_1_d1), .dp(1'b0));
  Seven_Seg_Hex seven_seg_hex_8 (.d(calculator_1_d0), .dp(1'b0));

  // Notes on the sheet:
  //   clk: Hz: 100
endmodule

/* Code of encoder:
module encoder(
	input P0,P1,P2,P3,P4,P5,P6,P7,P8,P9,PA,PB,PC,PD,PE,PF,
	input CLK,
	output reg [3:0] DATA,
	output reg DA);
	
	wire button;

	assign button = P0|P1|P2|P3|P4|P5|P6|P7|P8|P9|PA|PB|PC|PD|PE|PF;

	always @(posedge CLK)
		begin
			if(button)
			begin
				DA <= 1'b1;
				if      (P0) DATA <= 4'b0000;
				else if (P1) DATA <= 4'b0001;
				else if (P2) DATA <= 4'b0010;
				else if (P3) DATA <= 4'b0011;
				else if (P4) DATA <= 4'b0100;
				else if (P5) DATA <= 4'b0101;
				else if (P6) DATA <= 4'b0110;
				else if (P7) DATA <= 4'b0111;
				else if (P8) DATA <= 4'b1000;
				else if (P9) DATA <= 4'b1001;
				else if (PA) DATA <= 4'b1010;
				else if (PB) DATA <= 4'b1011;
				else if (PC) DATA <= 4'b1100;
				else if (PD) DATA <= 4'b1101;
				else if (PE) DATA <= 4'b1110;
				else if (PF) DATA <= 4'b1111;
			end
			else
			begin
				DA <= 1'b0;
			end				
		end			
endmodule
*/
