// Digital circuit selector.dig as structural Verilog
module selector (
  input  [3:0] d,
  output _0_9,
  output clear,
  output sum,
  output sum_clear
);

  wire decoder_1_out_0, decoder_1_out_1, decoder_1_out_2, decoder_1_out_3, decoder_1_out_4, decoder_1_out_5,
       decoder_1_out_6, decoder_1_out_7, decoder_1_out_8, decoder_1_out_9;

  Decoder #(.Selector_Bits(4)) decoder_1 (
    .sel(d), .out_0(decoder_1_out_0), .out_1(decoder_1_out_1), .out_2(decoder_1_out_2),
    .out_3(decoder_1_out_3), .out_4(decoder_1_out_4), .out_5(decoder_1_out_5), .out_6(decoder_1_out_6),
    .out_7(decoder_1_out_7), .out_8(decoder_1_out_8), .out_9(decoder_1_out_9), .out_14(clear), .out_15(sum));  // open: out_10, out_11, out_12, out_13
  or or_1 (_0_9, decoder_1_out_0, decoder_1_out_1, decoder_1_out_2, decoder_1_out_3, decoder_1_out_4, decoder_1_out_5, decoder_1_out_6, decoder_1_out_7, decoder_1_out_8, decoder_1_out_9);
  or or_2 (sum_clear, sum, clear);
endmodule
