// Digital circuit summer.dig as structural Verilog
module summer (
  input  [31:0] X,
  input  [31:0] Y,
  output [31:0] sum
);

  wire bcdadder_1_cout, bcdadder_2_cout, bcdadder_3_cout, bcdadder_4_cout, bcdadder_5_cout, bcdadder_6_cout,
       bcdadder_7_cout;

  BCDadder bcdadder_1 (.A(X[3:0]), .B(Y[3:0]), .Cin(1'b0), .Cout(bcdadder_1_cout), .sum(sum[3:0]));
  BCDadder bcdadder_2 (.A(X[7:4]), .B(Y[7:4]), .Cin(bcdadder_1_cout), .Cout(bcdadder_2_cout), .sum(sum[7:4]));
  BCDadder bcdadder_3 (.A(X[11:8]), .B(Y[11:8]), .Cin(bcdadder_2_cout), .Cout(bcdadder_3_cout), .sum(sum[11:8]));
  BCDadder bcdadder_4 (.A(X[15:12]), .B(Y[15:12]), .Cin(bcdadder_3_cout), .Cout(bcdadder_4_cout), .sum(sum[15:12]));
  BCDadder bcdadder_5 (.A(X[19:16]), .B(Y[19:16]), .Cin(bcdadder_4_cout), .Cout(bcdadder_5_cout), .sum(sum[19:16]));
  BCDadder bcdadder_6 (.A(X[23:20]), .B(Y[23:20]), .Cin(bcdadder_5_cout), .Cout(bcdadder_6_cout), .sum(sum[23:20]));
  BCDadder bcdadder_7 (.A(X[27:24]), .B(Y[27:24]), .Cin(bcdadder_6_cout), .Cout(bcdadder_7_cout), .sum(sum[27:24]));
  BCDadder bcdadder_8 (.A(X[31:28]), .B(Y[31:28]), .Cin(bcdadder_7_cout), .sum(sum[31:28]));  // open: Cout
endmodule
