// Digital circuit abs.dig as structural Verilog
module abs (
  input  [3:0] in,
  output sign,
  output [3:0] out
);

  wire [3:0] xor_2_out;

  xor xor_1 (xor_2_out[0], in[3], in[0]);
  xor xor_2 (xor_2_out[1], in[3], in[1]);
  xor xor_3 (xor_2_out[2], in[3], in[2]);
  xor xor_4 (xor_2_out[3], in[3], in[3]);
  Add #(.Bits(4)) add_1 (.a({3'b000, in[3]}), .b(xor_2_out), .c_i(1'b0), .s(out));  // open: c_o

  assign sign = in[3];
endmodule
