// Digital circuit binary2bcd.dig as structural Verilog
module binary2bcd (
  input  [7:0] Input,
  output [3:0] units,
  output [3:0] tens,
  output [3:0] hundreds
);

  wire add3_1_s0, add3_1_s1, add3_1_s2, add3_1_s3, add3_2_s0, add3_2_s1, add3_2_s2, add3_4_s0, add3_4_s1,
       add3_4_s2, add3_4_s3, add3_5_s0, add3_5_s1, add3_5_s2, add3_5_s3, add3_6_s0, add3_6_s1, add3_6_s2,
       add3_6_s3;

  add3 add3_1 (
    .A0(Input[5]), .A1(Input[6]), .A2(Input[7]), .A3(1'b0), .S0(add3_1_s0), .S1(add3_1_s1), .S2(add3_1_s2),
    .S3(add3_1_s3));
  add3 add3_2 (
    .A0(add3_5_s3), .A1(add3_4_s3), .A2(add3_1_s3), .A3(1'b0), .S0(add3_2_s0), .S1(add3_2_s1),
    .S2(add3_2_s2), .S3(hundreds[1]));
  add3 add3_3 (
    .A0(add3_6_s3), .A1(add3_2_s0), .A2(add3_2_s1), .A3(add3_2_s2), .S0(tens[1]), .S1(tens[2]), .S2(tens[3]),
    .S3(hundreds[0]));
  add3 add3_4 (
    .A0(Input[4]), .A1(add3_1_s0), .A2(add3_1_s1), .A3(add3_1_s2), .S0(add3_4_s0), .S1(add3_4_s1),
    .S2(add3_4_s2), .S3(add3_4_s3));
  add3 add3_5 (
    .A0(Input[3]), .A1(add3_4_s0), .A2(add3_4_s1), .A3(add3_4_s2), .S0(add3_5_s0), .S1(add3_5_s1),
    .S2(add3_5_s2), .S3(add3_5_s3));
  add3 add3_6 (
    .A0(Input[2]), .A1(add3_5_s0), .A2(add3_5_s1), .A3(add3_5_s2), .S0(add3_6_s0), .S1(add3_6_s1),
    .S2(add3_6_s2), .S3(add3_6_s3));
  add3 add3_7 (
    .A0(Input[1]), .A1(add3_6_s0), .A2(add3_6_s1), .A3(add3_6_s2), .S0(units[1]), .S1(units[2]),
    .S2(units[3]), .S3(tens[0]));

  assign hundreds[3:2] = 2'b00;
  assign units[0] = Input[0];
endmodule
