// Digital circuit signed_multiplier.dig as structural Verilog
module signed_multiplier (
  input  in_1,
  input  in_2,
  input  in_3,
  input  in_4,
  input  in_5,
  input  in_6,
  input  in_7,
  input  in_8
);

  wire abs_1_sign;
  wire [3:0] abs_1_out, binary2bcd_1_hundreds, binary2bcd_1_tens, binary2bcd_1_units, binary2bcd_2_hundreds,
       binary2bcd_2_tens, binary2bcd_2_units, unsignedbcd_1_tens, unsignedbcd_1_units, unsignedbcd_2_tens,
       unsignedbcd_2_units, unsignedbcd_3_tens, unsignedbcd_3_units;
  wire [7:0] mul_1_mul, mul_2_mul;

  Seven_Seg_Hex seven_seg_hex_1 (.d(unsignedbcd_1_tens), .dp(1'b0));
  Seven_Seg_Hex seven_seg_hex_2 (.d(unsignedbcd_2_tens), .dp(1'b0));
  Seven_Seg_Hex seven_seg_hex_3 (.d(unsignedbcd_1_units), .dp(1'b0));
  unsignedBCD unsignedbcd_1 (.Input({in_5, in_6, in_7, in_8}), .tens(unsignedbcd_1_tens), .units(unsignedbcd_1_units));
  Seven_Seg_Hex seven_seg_hex_4 (.d(unsignedbcd_2_units), .dp(1'b0));
  unsignedBCD unsignedbcd_2 (.Input({in_5, in_6, in_7, in_8}), .tens(unsignedbcd_2_tens), .units(unsignedbcd_2_units));
  Seven_Seg seven_seg_1 (.a(1'b0), .b(1'b0), .c(1'b0), .d(1'b0), .e(1'b0), .f(1'b0), .g(abs_1_sign), .dp(1'b0));
  abs abs_1 (.in({in_1, in_2, in_3, in_4}), .sign(abs_1_sign), .out(abs_1_out));
  Seven_Seg_Hex seven_seg_hex_5 (.d(unsignedbcd_3_tens), .dp(1'b0));
  Seven_Seg_Hex seven_seg_hex_6 (.d(abs_1_out), .dp(1'b0));
  Seven_Seg_Hex seven_seg_hex_7 (.d(unsignedbcd_3_units), .dp(1'b0));
  unsignedBCD unsignedbcd_3 (.Input({in_1, in_2, in_3, in_4}), .tens(unsignedbcd_3_tens), .units(unsignedbcd_3_units));
  Seven_Seg seven_seg_2 (.a(1'b0), .b(1'b0), .c(1'b0), .d(1'b0), .e(1'b0), .f(1'b0), .g(abs_1_sign), .dp(1'b0));
  binary2bcd binary2bcd_1 (
    .Input(mul_1_mul), .units(binary2bcd_1_units), .tens(binary2bcd_1_tens), .hundreds(binary2bcd_1_hundreds));
  Mul #(.Bits(4)) mul_1 (.a({in_5, in_6, in_7, in_8}), .b(abs_1_out), .mul(mul_1_mul));
  binary2bcd binary2bcd_2 (
    .Input(mul_2_mul), .units(binary2bcd_2_units), .tens(binary2bcd_2_tens), .hundreds(binary2bcd_2_hundreds));
  Mul #(.Bits(4)) mul_2 (.a({in_5, in_6, in_7, in_8}), .b({in_1, in_2, in_3, in_4}), .mul(mul_2_mul));
  Seven_Seg_Hex seven_seg_hex_8 (.d(binary2bcd_1_hundreds), .dp(1'b0));
  Seven_Seg_Hex seven_seg_hex_9 (.d(binary2bcd_2_hundreds), .dp(1'b0));
  Seven_Seg_Hex seven_seg_hex_10 (.d(binary2bcd_1_tens), .dp(1'b0));
  Seven_Seg_Hex seven_seg_hex_11 (.d(binary2bcd_2_tens), .dp(1'b0));
  Seven_Seg_Hex seven_seg_hex_12 (.d(binary2bcd_1_units), .dp(1'b0));
  Seven_Seg_Hex seven_seg_hex_13 (.d(binary2bcd_2_units), .dp(1'b0));

  // Notes on the sheet:
  //   x
  //   =
endmodule
