// Digital circuit unsignedBCD.dig as structural Verilog
module unsignedBCD (
  input  [3:0] Input,
  output [3:0] tens,
  output [3:0] units
);

  wire add3_1_s0, add3_1_s1, add3_1_s2, add3_3_s0, add3_3_s1, add3_3_s2, add3_3_s3, add3_4_s0, add3_4_s1,
       add3_4_s2, add3_4_s3;

  add3 add3_1 (
    .A0(add3_3_s3), .A1(1'b0), .A2(1'b0), .A3(1'b0), .S0(add3_1_s0), .S1(add3_1_s1), .S2(add3_1_s2));  // open: S3
  add3 add3_2 (
    .A0(add3_4_s3), .A1(add3_1_s0), .A2(add3_1_s1), .A3(add3_1_s2), .S0(tens[1]), .S1(tens[2]), .S2(tens[3]));  // open: S3
  add3 add3_3 (
    .A0(Input[3]), .A1(1'b0), .A2(1'b0), .A3(1'b0), .S0(add3_3_s0), .S1(add3_3_s1), .S2(add3_3_s2),
    .S3(add3_3_s3));
  add3 add3_4 (
    .A0(Input[2]), .A1(add3_3_s0), .A2(add3_3_s1), .A3(add3_3_s2), .S0(add3_4_s0), .S1(add3_4_s1),
    .S2(add3_4_s2), .S3(add3_4_s3));
  add3 add3_5 (
    .A0(Input[1]), .A1(add3_4_s0), .A2(add3_4_s1), .A3(add3_4_s2), .S0(units[1]), .S1(units[2]),
    .S2(units[3]), .S3(tens[0]));

  assign units[0] = Input[0];
endmodule
