// Digital circuit cntDECu.dig as structural Verilog
module cntDECu (
  input  CLK,
  input  LOAD0,
  input  CE,
  output [3:0] CNT,
  output EQ9
);

  wire and_1_out, and_2_out, and_3_out, and_4_out, and_5_out, and_6_out, and_7_out, and_8_out, d_ff_1_nq,
       d_ff_2_nq, d_ff_3_nq, d_ff_4_nq, multiplexer_1_out, multiplexer_2_out, multiplexer_3_out,
       multiplexer_4_out, nor_1_out;

  and and_1 (and_1_out, EQ9, CE);
  nor nor_1 (nor_1_out, and_1_out, LOAD0);
  and and_2 (and_2_out, multiplexer_1_out, nor_1_out);
  and and_3 (and_3_out, multiplexer_2_out, nor_1_out);
  and and_4 (and_4_out, multiplexer_3_out, nor_1_out);
  and and_5 (and_5_out, multiplexer_4_out, nor_1_out);
  D_FF d_ff_1 (.D(and_2_out), .C(CLK), .Q(CNT[0]), .nQ(d_ff_1_nq));
  D_FF d_ff_2 (.D(and_3_out), .C(CLK), .Q(CNT[1]), .nQ(d_ff_2_nq));
  D_FF d_ff_3 (.D(and_4_out), .C(CLK), .Q(CNT[2]), .nQ(d_ff_3_nq));
  D_FF d_ff_4 (.D(and_5_out), .C(CLK), .Q(CNT[3]), .nQ(d_ff_4_nq));
  Multiplexer multiplexer_1 (.sel(CE), .in_0(CNT[0]), .in_1(d_ff_1_nq), .out(multiplexer_1_out));
  Multiplexer multiplexer_2 (.sel(and_6_out), .in_0(CNT[1]), .in_1(d_ff_2_nq), .out(multiplexer_2_out));
  Multiplexer multiplexer_3 (.sel(and_7_out), .in_0(CNT[2]), .in_1(d_ff_3_nq), .out(multiplexer_3_out));
  Multiplexer multiplexer_4 (.sel(and_8_out), .in_0(CNT[3]), .in_1(d_ff_4_nq), .out(multiplexer_4_out));
  and and_6 (and_6_out, CNT[0], CE);
  and and_7 (and_7_out, CNT[1], and_6_out);
  and and_8 (and_8_out, CNT[2], and_7_out);
  and and_9 (EQ9, CNT[0], ~CNT[1], ~CNT[2], CNT[3]);  // And
endmodule
