// Digital circuit tally-2.dig as structural Verilog
module tally_2 (
  input  clk,
  input  reset,
  input  button,
  output [3:0] t10,
  output [3:0] t1
);

  wire and_1_out, and_2_out, and_3_out, cntdecu_2_eq9, d_ff_1_q, d_ff_2_q, d_ff_3_q, not_1_out, not_2_out,
       not_3_out, not_4_out, or_1_out;

  D_FF d_ff_1 (.D(t10[1]), .C(clk), .Q(d_ff_1_q));  // open: nQ
  D_FF d_ff_2 (.D(button), .C(clk), .Q(d_ff_2_q));  // open: nQ
  not not_1 (not_1_out, cntdecu_2_eq9);
  D_FF d_ff_3 (.D(cntdecu_2_eq9), .C(clk), .Q(d_ff_3_q));  // open: nQ
  not not_2 (not_2_out, d_ff_1_q);
  not not_3 (not_3_out, button);
  and and_1 (and_1_out, not_1_out, d_ff_3_q);
  and and_2 (and_2_out, t10[1], not_2_out);
  and and_3 (and_3_out, not_3_out, d_ff_2_q);
  not not_4 (not_4_out, reset);
  or or_1 (or_1_out, and_2_out, not_4_out);
  cntDECu cntdecu_1 (.CLK(clk), .LOAD0(or_1_out), .CE(and_1_out), .CNT(t10));  // open: EQ9
  cntDECu cntdecu_2 (.CLK(clk), .LOAD0(not_4_out), .CE(and_3_out), .CNT(t1), .EQ9(cntdecu_2_eq9));
endmodule
