// Digital circuit testbench.dig as structural Verilog
module testbench (
  input  _100_Hz
);

  wire COUNT_out, RESET_out;
  wire [3:0] tally_1_t1, tally_1_t10;

  Button #(.activeLow("true")) COUNT (.out(COUNT_out));
  Button #(.activeLow("true")) RESET (.out(RESET_out));
  tally tally_1 (.clk(_100_Hz), .reset(RESET_out), .button(COUNT_out), .t10(tally_1_t10), .t1(tally_1_t1));
  Seven_Seg_Hex seven_seg_hex_1 (.d(tally_1_t10), .dp(1'b0));
  Seven_Seg_Hex seven_seg_hex_2 (.d(tally_1_t1), .dp(1'b0));

  // Notes on the sheet:
  //   _100_Hz: Hz: 100
endmodule
